// Logisim project UD-Counter.circ as structural Verilog
module UD_Counter (
  input  S0,
  input  S1,
  input  I3,
  input  I2,
  input  I1,
  input  I0,
  output [3:0] out_7
);

  wire and_1_out, and_2_out, and_3_out, and_4_out, and_5_out, and_6_out, and_7_out, and_8_out, and_9_out,
       and_10_out, and_11_out, and_12_out, and_13_out, and_14_out, and_15_out, and_16_out, and_17_out,
       and_18_out, and_19_out, and_20_out, and_21_out, and_22_out, and_23_out, and_24_out, and_25_out,
       and_26_out, and_27_out, and_28_out, clock_1_out, controlled_buffer_1_out, controlled_buffer_2_out,
       controlled_buffer_4_out, controlled_buffer_6_out, not_1_out, not_2_out, not_3_out, not_4_out,
       not_5_out, not_6_out, not_7_out, not_8_out, not_9_out, not_10_out, not_11_out, not_12_out, not_13_out,
       not_14_out, not_15_out, not_16_out, not_17_out, not_18_out, not_19_out, not_20_out, not_21_out,
       not_22_out, not_23_out, not_24_out, not_25_out, not_26_out, not_27_out, not_28_out, not_29_out,
       not_30_out, not_31_out, not_32_out, not_33_out, not_34_out, not_35_out, not_36_out, not_37_out,
       not_38_out, not_39_out, not_40_out, not_41_out, not_42_out, not_43_out, not_44_out, not_45_out,
       not_46_out, not_47_out, not_48_out, not_49_out;
  wire [3:0] I0_q;

  assign controlled_buffer_1_out = not_1_out ? I0_q[3] : 1'bz;  // Controlled_Buffer controlled_buffer_1
  assign controlled_buffer_2_out = not_1_out ? I0_q[1] : 1'bz;  // Controlled_Buffer controlled_buffer_2
  not not_1 (not_1_out, and_1_out);
  and and_1 (and_1_out, S1, S0);
  assign controlled_buffer_1_out = and_1_out ? I3 : 1'bz;  // Controlled_Buffer controlled_buffer_3
  assign controlled_buffer_4_out = and_1_out ? I2 : 1'bz;  // Controlled_Buffer controlled_buffer_4
  assign controlled_buffer_4_out = not_1_out ? I0_q[2] : 1'bz;  // Controlled_Buffer controlled_buffer_5
  assign controlled_buffer_6_out = not_1_out ? I0_q[0] : 1'bz;  // Controlled_Buffer controlled_buffer_6
  assign controlled_buffer_2_out = and_1_out ? I1 : 1'bz;  // Controlled_Buffer controlled_buffer_7
  assign controlled_buffer_6_out = and_1_out ? I0 : 1'bz;  // Controlled_Buffer controlled_buffer_8
  not not_2 (not_2_out, S0);
  not not_3 (not_3_out, controlled_buffer_4_out);
  not not_4 (not_4_out, S0);
  not not_5 (not_5_out, controlled_buffer_6_out);
  not not_6 (not_6_out, S1);
  not not_7 (not_7_out, controlled_buffer_2_out);
  not not_8 (not_8_out, S1);
  not not_9 (not_9_out, controlled_buffer_1_out);
  not not_10 (not_10_out, controlled_buffer_4_out);
  not not_11 (not_11_out, controlled_buffer_2_out);
  not not_12 (not_12_out, controlled_buffer_6_out);
  not not_13 (not_13_out, S0);
  not not_14 (not_14_out, controlled_buffer_1_out);
  not not_15 (not_15_out, controlled_buffer_4_out);
  not not_16 (not_16_out, S1);
  not not_17 (not_17_out, S0);
  not not_18 (not_18_out, S0);
  not not_19 (not_19_out, controlled_buffer_2_out);
  not not_20 (not_20_out, controlled_buffer_6_out);
  not not_21 (not_21_out, S1);
  not not_22 (not_22_out, controlled_buffer_4_out);
  not not_23 (not_23_out, controlled_buffer_2_out);
  not not_24 (not_24_out, controlled_buffer_6_out);
  not not_25 (not_25_out, S0);
  not not_26 (not_26_out, controlled_buffer_4_out);
  not not_27 (not_27_out, controlled_buffer_2_out);
  not not_28 (not_28_out, S0);
  not not_29 (not_29_out, controlled_buffer_6_out);
  not not_30 (not_30_out, S1);
  not not_31 (not_31_out, S0);
  not not_32 (not_32_out, controlled_buffer_4_out);
  not not_33 (not_33_out, controlled_buffer_2_out);
  not not_34 (not_34_out, S1);
  not not_35 (not_35_out, controlled_buffer_2_out);
  not not_36 (not_36_out, controlled_buffer_6_out);
  not not_37 (not_37_out, S0);
  not not_38 (not_38_out, controlled_buffer_2_out);
  not not_39 (not_39_out, S1);
  not not_40 (not_40_out, S0);
  not not_41 (not_41_out, controlled_buffer_1_out);
  not not_42 (not_42_out, S1);
  not not_43 (not_43_out, S0);
  not not_44 (not_44_out, S1);
  not not_45 (not_45_out, S0);
  not not_46 (not_46_out, S1);
  not not_47 (not_47_out, controlled_buffer_6_out);
  not not_48 (not_48_out, S0);
  not not_49 (not_49_out, controlled_buffer_6_out);
  and and_2 (and_2_out, not_2_out, controlled_buffer_1_out, not_3_out);
  and and_3 (and_3_out, not_4_out, controlled_buffer_1_out, not_5_out);
  and and_4 (and_4_out, not_6_out, controlled_buffer_1_out, controlled_buffer_6_out);
  and and_5 (and_5_out, controlled_buffer_1_out, controlled_buffer_4_out, not_7_out);
  and and_6 (and_6_out, not_8_out, S0, not_9_out, not_10_out, not_11_out, not_12_out);
  and and_7 (and_7_out, S0, controlled_buffer_1_out, controlled_buffer_2_out);
  and and_8 (and_8_out, S1, not_13_out, not_14_out, controlled_buffer_4_out, controlled_buffer_2_out, controlled_buffer_6_out);
  and and_9 (and_9_out, S1, controlled_buffer_1_out, not_15_out);
  and and_10 (and_10_out, not_16_out, not_17_out, controlled_buffer_4_out);
  and and_11 (and_11_out, not_18_out, controlled_buffer_4_out, not_19_out);
  and and_12 (and_12_out, controlled_buffer_4_out, controlled_buffer_2_out, not_20_out);
  and and_13 (and_13_out, not_21_out, S0, not_22_out, not_23_out, not_24_out);
  and and_14 (and_14_out, S0, controlled_buffer_4_out, controlled_buffer_6_out);
  and and_15 (and_15_out, S1, not_25_out, not_26_out, controlled_buffer_2_out, controlled_buffer_6_out);
  and and_16 (and_16_out, S1, controlled_buffer_4_out, not_27_out);
  and and_17 (and_17_out, not_28_out, controlled_buffer_2_out, not_29_out);
  and and_18 (and_18_out, not_30_out, controlled_buffer_2_out, controlled_buffer_6_out);
  and and_19 (and_19_out, not_31_out, controlled_buffer_1_out, not_32_out, not_33_out, controlled_buffer_6_out);
  and and_20 (and_20_out, not_34_out, S0, not_35_out, not_36_out);
  and and_21 (and_21_out, S1, not_37_out, not_38_out, controlled_buffer_6_out);
  and and_22 (and_22_out, S1, S0, controlled_buffer_2_out);
  and and_23 (and_23_out, not_39_out, not_40_out, not_41_out, controlled_buffer_6_out);
  and and_24 (and_24_out, not_42_out, not_43_out, controlled_buffer_2_out, controlled_buffer_6_out);
  and and_25 (and_25_out, not_44_out, not_45_out, controlled_buffer_4_out, controlled_buffer_6_out);
  and and_26 (and_26_out, not_46_out, S0, not_47_out);
  and and_27 (and_27_out, S1, not_48_out, not_49_out);
  and and_28 (and_28_out, S1, S0, controlled_buffer_6_out);
  or or_1 (out_7[2], and_10_out, and_11_out, and_12_out, and_13_out, and_14_out, and_15_out, and_16_out);
  or or_2 (out_7[1], and_17_out, and_18_out, and_19_out, and_20_out, and_21_out, and_22_out);
  or or_3 (out_7[0], and_23_out, and_24_out, and_25_out, and_26_out, and_27_out, and_28_out);
  or or_4 (out_7[3], and_2_out, and_3_out, and_4_out, and_5_out, and_6_out, and_7_out, and_8_out, and_9_out);
  Hex_Digit_Display hex_digit_display_1 (.value(out_7));  // open: dp
  D_Flip_Flop u_I3 (.clk(clock_1_out), .D(out_7[3]), .Q(I0_q[3]), .en(1'b1));  // open: Qn, preset, reset
  D_Flip_Flop u_I2 (.clk(clock_1_out), .D(out_7[2]), .Q(I0_q[2]), .en(1'b1));  // open: Qn, preset, reset
  D_Flip_Flop u_I1 (.clk(clock_1_out), .D(out_7[1]), .Q(I0_q[1]), .en(1'b1));  // open: Qn, preset, reset
  D_Flip_Flop u_I0 (.clk(clock_1_out), .D(out_7[0]), .Q(I0_q[0]), .en(1'b1));  // open: Qn, preset, reset
  Clock clock_1 (.out(clock_1_out));

  // Notes on the sheet:
  //   I3
  //   I2
  //   I1
  //   I0
endmodule
