// Logisim project Decoder 2X4.circ as structural Verilog: 1 circuit, main circuit main
module main (
  input  I1,
  input  I0,
  input  I1_2,
  input  I0_2,
  input  Enable,
  input  I1_3,
  input  I0_3,
  input  Enable_2,
  input  Enable_3,
  output D0,
  output D1,
  output D0_2,
  output D2,
  output D1_2,
  output D2_2,
  output D3,
  output D3_2,
  output D0_3,
  output D1_3,
  output D2_3,
  output D3_3
);

  wire And__1_out, And__2_out, And__3_out, And__4_out, NAND_1_out, NAND_2_out, NAND_3_out, NAND_4_out,
       not_1_out, not_2_out, not_3_out, not_4_out, not_5_out, not_6_out, not_7_out, not_8_out,
       transistor_1_out, transistor_3_out, transistor_5_out, transistor_7_out, transistor_9_out,
       transistor_12_out, transistor_13_out, transistor_16_out, transistor_17_out, transistor_20_out,
       transistor_21_out, transistor_24_out, transistor_25_out, transistor_27_out, transistor_29_out,
       transistor_31_out, transistor_33_out, transistor_37_out, transistor_41_out, transistor_45_out;

  not not_1 (not_1_out, I1);
  not not_2 (not_2_out, I0);
  not not_3 (not_3_out, I1);
  not not_4 (not_4_out, I0);
  not not_5 (not_5_out, I1_3);
  not not_6 (not_6_out, I0_3);
  not not_7 (not_7_out, I1_3);
  not not_8 (not_8_out, I0_3);
  and And__1 (And__1_out, not_1_out, not_2_out);
  and And__2 (And__2_out, not_3_out, I0);
  and And__3 (And__3_out, I1, not_4_out);
  and And__4 (And__4_out, I1, I0);
  nand NAND_1 (NAND_1_out, not_5_out, not_6_out);
  nand NAND_2 (NAND_2_out, not_7_out, I0_3);
  nand NAND_3 (NAND_3_out, I1_3, not_8_out);
  nand NAND_4 (NAND_4_out, I1_3, I0_3);
  assign D1 = Enable ? And__2_out : 1'bz;  // Controlled_Buffer controlled_buffer_1
  assign D2 = Enable ? And__3_out : 1'bz;  // Controlled_Buffer controlled_buffer_2
  assign D3 = Enable ? And__4_out : 1'bz;  // Controlled_Buffer controlled_buffer_3
  assign D2_3 = Enable_2 ? ~NAND_3_out : 1'bz;  // Controlled_Inverter controlled_inverter_1
  assign D3_3 = Enable_2 ? ~NAND_4_out : 1'bz;  // Controlled_Inverter controlled_inverter_2
  assign D0 = Enable ? And__1_out : 1'bz;  // Controlled_Buffer controlled_buffer_4
  assign D0_3 = Enable_2 ? ~NAND_1_out : 1'bz;  // Controlled_Inverter controlled_inverter_3
  assign D1_3 = Enable_2 ? ~NAND_2_out : 1'bz;  // Controlled_Inverter controlled_inverter_4
  Transistor transistor_1 (.in(1'b1), .out(transistor_1_out), .gate(I1_2));
  Transistor #(.\type ("n")) transistor_2 (.in(1'b0), .out(transistor_1_out), .gate(I1_2));
  Transistor transistor_3 (.in(1'b1), .out(transistor_3_out), .gate(I0_2));
  Transistor #(.\type ("n")) transistor_4 (.in(1'b0), .out(transistor_3_out), .gate(I0_2));
  Transistor transistor_5 (.in(1'b1), .out(transistor_5_out), .gate(I1_2));
  Transistor #(.\type ("n")) transistor_6 (.in(1'b0), .out(transistor_5_out), .gate(I1_2));
  Transistor transistor_7 (.in(1'b1), .out(transistor_7_out), .gate(I0_2));
  Transistor #(.\type ("n")) transistor_8 (.in(1'b0), .out(transistor_7_out), .gate(I0_2));
  Transistor transistor_9 (.in(1'b1), .out(transistor_9_out), .gate(transistor_1_out));
  Transistor transistor_10 (.in(1'b1), .out(transistor_9_out), .gate(transistor_3_out));
  Transistor #(.\type ("n")) transistor_11 (.in(transistor_12_out), .out(transistor_9_out), .gate(transistor_1_out));
  Transistor #(.\type ("n")) transistor_12 (.in(1'b0), .out(transistor_12_out), .gate(transistor_3_out));
  Transistor transistor_13 (.in(1'b1), .out(transistor_13_out), .gate(transistor_5_out));
  Transistor transistor_14 (.in(1'b1), .out(transistor_13_out), .gate(I0_2));
  Transistor #(.\type ("n")) transistor_15 (.in(transistor_16_out), .out(transistor_13_out), .gate(transistor_5_out));
  Transistor #(.\type ("n")) transistor_16 (.in(1'b0), .out(transistor_16_out), .gate(I0_2));
  Transistor transistor_17 (.in(1'b1), .out(transistor_17_out), .gate(I1_2));
  Transistor transistor_18 (.in(1'b1), .out(transistor_17_out), .gate(transistor_7_out));
  Transistor #(.\type ("n")) transistor_19 (.in(transistor_20_out), .out(transistor_17_out), .gate(I1_2));
  Transistor #(.\type ("n")) transistor_20 (.in(1'b0), .out(transistor_20_out), .gate(transistor_7_out));
  Transistor transistor_21 (.in(1'b1), .out(transistor_21_out), .gate(I1_2));
  Transistor transistor_22 (.in(1'b1), .out(transistor_21_out), .gate(I0_2));
  Transistor #(.\type ("n")) transistor_23 (.in(transistor_24_out), .out(transistor_21_out), .gate(I1_2));
  Transistor #(.\type ("n")) transistor_24 (.in(1'b0), .out(transistor_24_out), .gate(I0_2));
  Transistor transistor_25 (.in(1'b1), .out(transistor_25_out), .gate(transistor_9_out));
  Transistor #(.\type ("n")) transistor_26 (.in(1'b0), .out(transistor_25_out), .gate(transistor_9_out));
  Transistor transistor_27 (.in(1'b1), .out(transistor_27_out), .gate(transistor_13_out));
  Transistor #(.\type ("n")) transistor_28 (.in(1'b0), .out(transistor_27_out), .gate(transistor_13_out));
  Transistor transistor_29 (.in(1'b1), .out(transistor_29_out), .gate(transistor_17_out));
  Transistor #(.\type ("n")) transistor_30 (.in(1'b0), .out(transistor_29_out), .gate(transistor_17_out));
  Transistor transistor_31 (.in(1'b1), .out(transistor_31_out), .gate(transistor_21_out));
  Transistor #(.\type ("n")) transistor_32 (.in(1'b0), .out(transistor_31_out), .gate(transistor_21_out));
  Transistor transistor_33 (.in(1'b1), .out(transistor_33_out), .gate(Enable_3));
  Transistor #(.\type ("n")) transistor_34 (.in(1'b0), .out(transistor_33_out), .gate(Enable_3));
  Transistor transistor_35 (.in(transistor_25_out), .out(D0_2), .gate(transistor_33_out));
  Transistor #(.\type ("n"), .gate("br")) transistor_36 (.in(transistor_25_out), .out(D0_2), .gate(Enable_3));
  Transistor transistor_37 (.in(1'b1), .out(transistor_37_out), .gate(Enable_3));
  Transistor #(.\type ("n")) transistor_38 (.in(1'b0), .out(transistor_37_out), .gate(Enable_3));
  Transistor transistor_39 (.in(transistor_27_out), .out(D1_2), .gate(transistor_37_out));
  Transistor #(.\type ("n"), .gate("br")) transistor_40 (.in(transistor_27_out), .out(D1_2), .gate(Enable_3));
  Transistor transistor_41 (.in(1'b1), .out(transistor_41_out), .gate(Enable_3));
  Transistor #(.\type ("n")) transistor_42 (.in(1'b0), .out(transistor_41_out), .gate(Enable_3));
  Transistor transistor_43 (.in(transistor_29_out), .out(D2_2), .gate(transistor_41_out));
  Transistor #(.\type ("n"), .gate("br")) transistor_44 (.in(transistor_29_out), .out(D2_2), .gate(Enable_3));
  Transistor transistor_45 (.in(1'b1), .out(transistor_45_out), .gate(Enable_3));
  Transistor #(.\type ("n")) transistor_46 (.in(1'b0), .out(transistor_45_out), .gate(Enable_3));
  Transistor transistor_47 (.in(transistor_31_out), .out(D3_2), .gate(transistor_45_out));
  Transistor #(.\type ("n"), .gate("br")) transistor_48 (.in(transistor_31_out), .out(D3_2), .gate(Enable_3));

  // Notes on the sheet:
  //   Decoder 2X4 (using AND-NOT-BUFFER) | Gate Abstract
  //   Decoder 2X4 (using NAND-NOT-BUFFER) | Gate Abstract
  //   Decoder 2X4 | Transistor Level
endmodule
