// Logisim project Sudo-Random-Circuit.circ as structural Verilog: 1 circuit, main circuit main
module main (
  input  [3:0] in_1,
  input  in_2
);

  wire clock_1_out, multiplexer_1_out, multiplexer_2_out, multiplexer_3_out, multiplexer_4_out, xor_1_out;
  wire [3:0] d_ff_4_q;

  Clock clock_1 (.out(clock_1_out));
  Multiplexer #(.enable("false")) multiplexer_1 (.in0(xor_1_out), .in1(in_1[3]), .out(multiplexer_1_out), .sel(in_2));
  Multiplexer #(.enable("false")) multiplexer_2 (.in0(d_ff_4_q[3]), .in1(in_1[2]), .out(multiplexer_2_out), .sel(in_2));
  Multiplexer #(.enable("false")) multiplexer_3 (.in0(d_ff_4_q[2]), .in1(in_1[1]), .out(multiplexer_3_out), .sel(in_2));
  Multiplexer #(.enable("false")) multiplexer_4 (.in0(d_ff_4_q[1]), .in1(in_1[0]), .out(multiplexer_4_out), .sel(in_2));
  D_Flip_Flop d_ff_1 (.clk(clock_1_out), .D(multiplexer_1_out), .Q(d_ff_4_q[3]), .en(1'b1));  // open: Qn, preset, reset
  D_Flip_Flop d_ff_2 (.clk(clock_1_out), .D(multiplexer_2_out), .Q(d_ff_4_q[2]), .en(1'b1));  // open: Qn, preset, reset
  D_Flip_Flop d_ff_3 (.clk(clock_1_out), .D(multiplexer_3_out), .Q(d_ff_4_q[1]), .en(1'b1));  // open: Qn, preset, reset
  D_Flip_Flop d_ff_4 (.clk(clock_1_out), .D(multiplexer_4_out), .Q(d_ff_4_q[0]), .en(1'b1));  // open: Qn, preset, reset
  xor xor_1 (xor_1_out, d_ff_4_q[3], d_ff_4_q[0]);
  Hex_Digit_Display hex_digit_display_1 (.value(d_ff_4_q));  // open: dp

  // Notes on the sheet:
  //   f(x) = x(4) + x + 1
  //   I3
  //   I2
  //   I1
  //   I0
endmodule
